# Fritzing sketch ArduinoMega_SW_SPI_BME280 (saved by Fritzing 0.9.3b)

parts:
  Part1 = Arduino Mega 2560 (Rev3)
  Part2 = Adafruit BME280

nets:
  GND: Part1.GND, Part2.GND
  N1: Part1.D13_PWM, Part2.SCK/SCL
  N2: Part1.D12_PWM, Part2.SDO/ADR
  N3: Part1.D11_PWM, Part2.SDI/SDA
  N4: Part1.D10_PWM, Part2.CS
  5V: Part1.5V, Part2.VIN

notes:
  Software SPI

custom parts:
  Adafruit BME280: Bosch has stepped up their game with their new BME280 sensor, an environmental sensor with temperature, barometric pressure and humidity! This sensor is great for all sorts of weather/environmental sensing and can even be used in both I2C and SPI! This precision sensor from Bosch is the best low-cost sensing solution for measuring humidity with ±3% accuracy, barometric pressure with ±1 hPa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
